// Logisim project ejercicio10.circ as structural Verilog: 1 circuit, main circuit main
module main (
  input  a0,
  input  a1,
  input  b0,
  input  b1,
  output c3,
  output c2,
  output c1,
  output c0
);

  wire adder_2_cout, and_1_out, and_2_out, and_3_out;

  and and_1 (and_1_out, a1, b0);
  Adder #(.width(1)) adder_1 (.a(adder_2_cout), .b(and_1_out), .out(c2), .cout(c3));  // open: cin
  and and_2 (and_2_out, a0, b0);
  and and_3 (and_3_out, a1, b0);
  Adder #(.width(1)) adder_2 (.a(and_2_out), .b(and_3_out), .out(c1), .cout(adder_2_cout));  // open: cin
  and and_4 (c0, a0, b1);
endmodule
