// Logisim project ejercicio3.circ as structural Verilog: 1 circuit, main circuit main
module main (
  input  d0,
  input  d1,
  input  d2,
  input  d3,
  input  d4,
  input  d5,
  input  d6,
  input  d7,
  output a0,
  output a1,
  output a2
);

  or or_1 (a0, d1, d3, d5, d7);
  or or_2 (a1, d2, d3, d6, d7);
  or or_3 (a2, d4, d5, d6, d7);
endmodule
