// Logisim project ejercicio4.circ as structural Verilog: 1 circuit, main circuit main
module main (
  input  s,
  input  I1,
  input  I0,
  output F
);

  wire and_1_out, and_2_out, not_1_out;

  not not_1 (not_1_out, s);
  and and_1 (and_1_out, not_1_out, I0);
  and and_2 (and_2_out, s, I1);
  or or_1 (F, and_1_out, and_2_out);
endmodule
