// Logisim project ejercicio5.circ as structural Verilog: 1 circuit, main circuit main
module main (
  input  I7,
  input  I6,
  input  I5,
  input  I4,
  input  I3,
  input  I2,
  input  I1,
  input  I0,
  input  I15,
  input  I14,
  input  I13,
  input  I12,
  input  I11,
  input  I10,
  input  I9,
  input  I8,
  input  S3,
  input  S2,
  input  S1,
  input  S0,
  output out_21
);

  wire multiplexer_1_out, multiplexer_2_out;

  Multiplexer #(.select(3)) multiplexer_1 (
    .in0(I0), .in1(I1), .in2(I2), .in3(I3), .in4(I4), .in5(I5), .in6(I6), .in7(I7), .out(multiplexer_1_out),
    .sel({S2, S1, S0}));
  Multiplexer #(.select(3)) multiplexer_2 (
    .in0(I8), .in1(I9), .in2(I10), .in3(I11), .in4(I12), .in5(I13), .in6(I14), .in7(I15),
    .out(multiplexer_2_out), .sel({S2, S1, S0}));
  Multiplexer multiplexer_3 (.in0(multiplexer_1_out), .in1(multiplexer_2_out), .out(out_21), .sel(S3));
endmodule
