// Logisim project ejercicio6.circ as structural Verilog: 1 circuit, main circuit main
module main (
  input  a,
  input  b,
  output S,
  output C
);

  xor xor_1 (S, a, b);
  and and_1 (C, a, b);
endmodule
