// Logisim project ejercicio9.circ as structural Verilog: 1 circuit, main circuit main
module main (
  input  a3,
  input  a2,
  input  a1,
  input  a0,
  input  b3,
  input  b2,
  input  b1,
  input  b0,
  input  sumador_restador,
  output r4,
  output r3,
  output r2,
  output r1,
  output r0
);

  wire adder_1_cout, adder_2_cout, adder_3_cout, xor_1_out, xor_2_out, xor_3_out, xor_4_out;

  xor xor_1 (xor_1_out, b3, sumador_restador);
  xor xor_2 (xor_2_out, b2, sumador_restador);
  xor xor_3 (xor_3_out, b1, sumador_restador);
  xor xor_4 (xor_4_out, b0, sumador_restador);
  Adder #(.width(1)) adder_1 (.a(a0), .b(xor_4_out), .out(r0), .cout(adder_1_cout));  // open: cin
  Adder #(.width(1)) adder_2 (.a(a1), .b(xor_3_out), .out(r1), .cin(adder_1_cout), .cout(adder_2_cout));
  Adder #(.width(1)) adder_3 (.a(a2), .b(xor_2_out), .out(r2), .cin(adder_2_cout), .cout(adder_3_cout));
  Adder #(.width(1)) adder_4 (.a(a3), .b(xor_1_out), .out(r3), .cin(adder_3_cout), .cout(r4));
endmodule
