// Logisim project ej7rehacer.circ as structural Verilog: 1 circuit, main circuit main
module main (
  input  I7,
  input  I6,
  input  I5,
  input  I4,
  input  I3,
  input  I2,
  input  I1,
  input  I0,
  input  S2,
  input  S1,
  input  S0,
  output out_12
);

  wire multiplexer_1_out, multiplexer_2_out;

  Multiplexer #(.select(2)) multiplexer_1 (
    .in0(I0), .in1(I1), .in2(I2), .in3(I3), .out(multiplexer_1_out), .sel({S1, S0}));
  Multiplexer #(.select(2)) multiplexer_2 (
    .in0(I4), .in1(I5), .in2(I6), .in3(I7), .out(multiplexer_2_out), .sel({S1, S0}));
  Multiplexer multiplexer_3 (.in0(multiplexer_1_out), .in1(multiplexer_2_out), .out(out_12), .sel(S2));
endmodule
