// Logisim project ej8.circ as structural Verilog: 1 circuit, main circuit main
module main (
  input  a1,
  input  a0,
  input  b1,
  input  b0,
  output r2,
  output r1,
  output r0
);

  wire adder_1_cout;

  Adder #(.width(1)) adder_1 (.a(a0), .b(b0), .out(r0), .cout(adder_1_cout));  // open: cin
  Adder #(.width(1)) adder_2 (.a(a1), .b(b1), .out(r1), .cin(adder_1_cout), .cout(r2));
endmodule
