// Logisim project ejemploClase1.circ as structural Verilog: 1 circuit, main circuit main
module main (
  input  x,
  input  y,
  output D0,
  output D1,
  output D2,
  output D3
);

  Decoder #(.select(2)) decoder_1 (.out0(D0), .out1(D1), .out2(D2), .out3(D3), .sel({x, y}));  // open: en
endmodule
